# Fritzing sketch Geral (saved by Fritzing 0.9.5d)
breadboards: 1

parts:
  Componente1 = Arduino Uno (Rev3)
  Componente2 = Módulo Relé
  VALVE1 = Plastic Solenoid Valve
  Componente3 = Módulo Relé
  Componente4 = Módulo Relé
  VALVE2 = Plastic Solenoid Valve
  ZS-042_RTC1 = ZS-042 RTC Module
  LED1 = LEDs [package=led10mm]
  Componente5 = Módulo Relé

nets:
  N1: Componente1.D10_PWM/SS, Componente5.In
  N2: Componente1.D11_PWM/MOSI, Componente4.In
  N3: Componente1.D12/MISO, Componente3.In
  N4: Componente1.D13/SCK, Componente2.In
  N5: Componente1.A4/SDA, ZS-042_RTC1.SDA
  N6: Componente1.A5/SCL, ZS-042_RTC1.SCL
  5V: Componente1.5V, Componente2.5V, Componente3.5V, Componente4.5V, ZS-042_RTC1.VCC, Componente5.5V
  GND: Componente1.GND, Componente2.GND, Componente3.GND, Componente4.GND, ZS-042_RTC1.GND, Componente5.GND
  N7: Componente2.NA, VALVE1.no_name_yet#2
  N8: Componente3.NF, VALVE2.no_name_yet#2
  N9: Componente4.NA, LED1.C

custom parts:
  Módulo Relé: Este modulo pode ser usado em diversos projetos afim de acionar cargas de até 250VAC @ 7A ou 125VAC @ 10A. Pode ser usado para controlar luzes, equipamentos ligados a rede elétrica, motores, etc. Você pode fazer uma ponte-H baseada em relés com alguns destes módulos.
  LEDs: LEDs Standard schematic elements and footprints for 5mm, 3mm, 1206, and 0603 sized LEDs. 5mm - Spark Fun Electronics SKU : COM-00529 (and others)
